# Fritzing sketch step_6 (saved by Fritzing 0.9.3b)
breadboards: 1

parts:
  U1 = ATTiny84 [package=dip]
  Part1 = Arduino Uno (Rev3) - ICSP

nets:
  N1: U1.pin1, Part1.5V
  N2: U1.pin4, Part1.D10_PWM/SS
  N3: U1.pin7, Part1.D11_PWM/MOSI
  N4: U1.pin8, Part1.D12/MISO
  N5: U1.pin9, Part1.D13/SCK
  N6: U1.pin14, Part1.GND

custom parts:
  ATTiny84: Atmel ATTiny84 processor. 8 ADC pins, 4 PWM pins. Available in either 10MHz or 20MHz. The last 2 pin numbers refer to arduino. D6 = Arduino 6, A6 = Arduino A6 example: PA6 (SDA/MOSI/OC1A/DI/AD6/PCINT6/D6/A6) NOTE: This part is diagrammed to suit the MIT HLT ATTiny84 core at https://github.com/damellis/attiny/
