# Fritzing sketch stripboard_plan copy (saved by Fritzing 0.9.3b)
stripboards: 1

parts:
  R4 = Resistor [tolerance=±5% resistance=62 package="0805 [SMD]"]  # not connected
  Q2 = NPN-Transistor [package="TO92 [THT]"]
  R5 = Resistor [tolerance=±5% resistance=220 package="1206 [SMD]"]
  R6 = Resistor [tolerance=±5% resistance=220 package="1206 [SMD]"]
  LED4 = LED - 5mm [color="White (4500K)" package="5 mm [THT]"]
  Q3 = NPN-Transistor [package="TO92 [THT]"]
  LED5 = LED - 5mm [color="White (4500K)" package="5 mm [THT]"]
  R7 = Resistor [tolerance=±5% resistance=62 package="0805 [SMD]"]

nets:
  N1: Q2.E, LED5.cathode
  N2: Q2.B, R5.Pin_0
  N3: R5.Pin_1, Q3.C
  N4: R6.Pin_0, Q3.B
  N5: LED4.cathode, Q3.E
  N6: LED4.anode, R7.Pin_0
