# Fritzing sketch stripboard_plan copy2 (saved by Fritzing 0.9.3b)
stripboards: 1

parts:
  R9 = Resistor [tolerance=±5% resistance=62 package="0805 [SMD]"]
  R5 = Resistor [tolerance=±5% resistance=2.2k package="1206 [SMD]"]
  Q4 = NPN-Transistor [package="TO92 [THT]"]
  R10 = Resistor [tolerance=±5% resistance=62 package="0805 [SMD]"]
  R8 = Resistor [tolerance=±5% resistance=2.2k package="1206 [SMD]"]
  R6 = Resistor [tolerance=±5% resistance=2.2k package="1206 [SMD]"]
  Q5 = NPN-Transistor [package="TO92 [THT]"]
  R4 = Resistor [tolerance=±5% resistance=62 package="0805 [SMD]"]
  Q3 = NPN-Transistor [package="TO92 [THT]"]
  J3 = male pin header, 1 pin [form="♂ (male)"]
  R11 = Resistor [tolerance=±5% resistance=10k package="1206 [SMD]"]
  J2 = male pin header, 1 pin [form="♂ (male)"]
  U1 = ATTiny84 [package=dip]
  J4 = double row male pin header, 2 pins [form="♂ (male)"]
  J1 = male pin header, 2 pins [form="♂ (male)"]
  JS1 = Generic Jumper Shunt
  LED16 = LED - 5mm [color="White (4500K)" package="5 mm [THT]"]
  LED13 = LED - 5mm [color="White (4500K)" package="5 mm [THT]"]
  LED11 = LED - 5mm [color="White (4500K)" package="5 mm [THT]"]
  LED14 = LED - 5mm [color="White (4500K)" package="5 mm [THT]"]
  LED18 = LED - 5mm [color="White (4500K)" package="5 mm [THT]"]
  LED20 = LED - 5mm [color="White (4500K)" package="5 mm [THT]"]
  LED12 = LED - 5mm [color="White (4500K)" package="5 mm [THT]"]
  LED17 = LED - 5mm [color="White (4500K)" package="5 mm [THT]"]
  LED15 = LED - 5mm [color="White (4500K)" package="5 mm [THT]"]
  C1 = Ceramic Capacitor [capacitance=10µF package="0603 [SMD, multilayer]"]
  S1 = Pushbutton [package="[SMD]"]
  IC1 = Voltage Regulator [package=to220-igo]
  R13 = Rotary Potentiometer (Small) [maximum_resistance=100kΩ package=THT]
  R12 = Rotary Potentiometer (Small) [maximum_resistance=100kΩ package=THT]
  U2 = SWITCH_SPDT [package=kps-1290]
  BAT1 = BC9VPC [package=bc9vpc]

nets:
  N1: R9.Pin_0, LED16.anode, LED14.anode, LED15.anode
  N2: R9.Pin_1, U1.pin9, J1.pin1
  N3: R5.Pin_0, Q3.B
  N4: R5.Pin_1, U1.pin12
  N5: Q4.E, LED11.cathode, LED14.cathode, LED17.cathode
  N6: Q4.B, R6.Pin_0
  N7: Q4.C, Q5.C, Q3.C, R11.Pin_0, U1.pin14, J4.pin1, C1.1, IC1.IN, R13.leg1, R12.leg1, U2.S, BAT1.V-
  N8: R10.Pin_0, LED18.anode, LED20.anode, LED17.anode
  N9: R10.Pin_1, U1.pin8, J1.pin2
  N10: R8.Pin_0, Q5.B
  N11: R8.Pin_1, U1.pin13, J4.pin2
  N12: R6.Pin_1, U1.pin11
  N13: Q5.E, LED16.cathode, LED13.cathode, LED20.cathode
  N14: R4.Pin_0, LED13.anode, LED11.anode, LED12.anode
  N15: R4.Pin_1, U1.pin10
  N16: Q3.E, LED18.cathode, LED12.cathode, LED15.cathode
  N17: J3.pin1, U1.pin4
  N18: R11.Pin_1, U1.pin5, S1.Pin_1, S1.Pin_2
  N19: J2.pin1, U1.pin7, JS1.pin1, JS1.pin2, R12.wiper
  N20: U1.pin1, S1.Pin_3, S1.Pin_4, IC1.OUT, R13.leg2, R12.leg2
  N21: U1.pin6, R13.wiper
  N22: C1.0, IC1.GND, U2.P
  N23: U2.O, BAT1.V+

custom parts:
  ATTiny84: Atmel ATTiny84 processor. 8 ADC pins, 4 PWM pins. Available in either 10MHz or 20MHz. The last 2 pin numbers refer to arduino. D6 = Arduino 6, A6 = Arduino A6 example: PA6 (SDA/MOSI/OC1A/DI/AD6/PCINT6/D6/A6) NOTE: This part is diagrammed to suit the MIT HLT ATTiny84 core at https://github.com/damellis/attiny/
